# Fritzing sketch PlantWater (saved by Fritzing 1.0.2b)
breadboards: 1

parts:
  A1 = Particle - Photon2
  Grove1 = Grove Dust Sensor
  WATER_PUMP1 = water pump/motor  # not connected
  Chirp!_Soil_Moisture_Sensor1 = Chirp! Soil Moisture Sensor v2.7.3
  OLED_I2C1 = OLED 128x64 I2C Monochrome Display
  M1 = DHT11-Grove-Temperature-Sensor_1
  Grove_Relay1 = Grove Relay  # not connected
  R1 = Resistor [tolerance=±5% resistance=220 package="1206 [SMD]"]
  VCC1 = 4 x AAA Battery Mount
  Part1 = MQ-131 breakout

nets:
  VDD: A1.Pin_3, Grove1.NC, Chirp!_Soil_Moisture_Sensor1.Pin_1, OLED_I2C1.VDD, M1.connector2, Part1.VCC
  GND: A1.Pin_4, A1.Pin_30, A1.Pin_35, Grove1.SIG, Chirp!_Soil_Moisture_Sensor1.pin_5, OLED_I2C1.GND, M1.connector3, VCC1.-, Part1.GND
  N1: A1.Pin_5, Part1.AO
  N2: A1.Pin_7, Chirp!_Soil_Moisture_Sensor1.pin_2
  N3: A1.Pin_17, OLED_I2C1.SDA, M1.connector1
  N4: A1.Pin_18, OLED_I2C1.SCK, M1.connector0
  N5: A1.Pin_20, Grove1.VCC
  N6: A1.Pin_26, R1.Pin_1

custom parts:
  Particle - Photon2: The Photon 2 is a microcontroller and Wi-Fi networking developed by particle. Features: 802.11a/b/g/n Wi-Fi, 2.4 GHz and 5 GHz Integrated PCB antenna Integrated U.FL connector for external antenna Integrated RF switch BLE 5 using same antenna as Wi-Fi Realtek RTL8721DM MCU ARM Cortex M33 CPU, 200 MHz 2048 KB (2 MB) user application maximum size 3072 KB (3 MB) of RAM available to user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
  Grove Dust Sensor: PPD42 Grove Dust Sensor
  water pump/motor: WATER PUMP BY ARDUBLOCKTR
  Grove Relay: Relay, Grove connector.
  MQ-131 breakout: SKU: 101282
